// Logisim project hw5.circ as structural Verilog
module MyXOR (
  input  X,
  input  Y,
  output Z
);

  wire and_1_out, and_2_out, not_1_out, not_2_out, or_1_out;

  not not_1 (not_1_out, X);
  not not_2 (not_2_out, Y);
  and and_1 (and_1_out, X, Y);
  and and_2 (and_2_out, not_2_out, not_1_out);
  or or_1 (or_1_out, and_1_out, and_1_out, and_2_out, and_2_out);
  not not_3 (Z, or_1_out);

  // Notes on the sheet:
  //   Here is a location to build an XOR circuit
  //   You can follow the tutorial (Help menu - "tutorial") or work on your own...
endmodule

module FullAdder (
  input  X,
  input  Y,
  input  CarryIn,
  output sum,
  output CarryOut
);

  wire and_1_out, and_2_out, and_3_out, and_4_out, and_5_out, and_6_out, and_7_out, and_8_out, not_1_out,
       not_2_out, not_3_out;

  not not_1 (not_1_out, X);
  not not_2 (not_2_out, Y);
  not not_3 (not_3_out, CarryIn);
  and and_1 (and_1_out, not_1_out, not_2_out, CarryIn);
  and and_2 (and_2_out, not_1_out, Y, not_3_out, not_3_out);
  and and_3 (and_3_out, X, not_2_out, not_3_out);
  and and_4 (and_4_out, Y, X, CarryIn);
  and and_5 (and_5_out, not_1_out, Y, CarryIn);
  and and_6 (and_6_out, X, not_2_out, CarryIn);
  and and_7 (and_7_out, X, Y, not_3_out);
  and and_8 (and_8_out, X, Y, CarryIn);
  or or_1 (sum, and_1_out, and_2_out, and_3_out, and_4_out);
  or or_2 (CarryOut, and_5_out, and_6_out, and_7_out, and_8_out);
endmodule

module _4_bit_Ripple_Carry_Adder (
  input  Y3,
  input  Y2,
  input  Y1,
  input  Y0,
  input  X3,
  input  X2,
  input  X1,
  input  X0,
  output Sum4,
  output Sum3,
  output Sum2,
  output Sum1,
  output Sum0
);

  wire fulladder_2_carryout, fulladder_3_carryout, fulladder_4_carryout;

  FullAdder fulladder_1 (.X(X3), .Y(Y3), .CarryIn(fulladder_2_carryout), .sum(Sum3), .CarryOut(Sum4));
  FullAdder fulladder_2 (.X(X2), .Y(Y2), .CarryIn(fulladder_3_carryout), .sum(Sum2), .CarryOut(fulladder_2_carryout));
  FullAdder fulladder_3 (.X(X1), .Y(Y1), .CarryIn(fulladder_4_carryout), .sum(Sum1), .CarryOut(fulladder_3_carryout));
  FullAdder fulladder_4 (.X(X0), .Y(Y0), .CarryIn(1'b0), .sum(Sum0), .CarryOut(fulladder_4_carryout));
endmodule

module _4_bit_Multiplier (
  input  Y3,
  input  Y2,
  input  Y1,
  input  Y0,
  input  X3,
  input  X2,
  input  X1,
  input  X0,
  output Z7,
  output Z6,
  output Z5,
  output Z4,
  output Z3,
  output Z2,
  output Z1,
  output Z0
);

  wire and_1_out, n4_bit_ripple_carry_adder_1_sum1, n4_bit_ripple_carry_adder_1_sum2,
       n4_bit_ripple_carry_adder_1_sum3, n4_bit_ripple_carry_adder_1_sum4, n4_bit_ripple_carry_adder_3_sum1,
       n4_bit_ripple_carry_adder_3_sum2, n4_bit_ripple_carry_adder_3_sum3, n4_bit_ripple_carry_adder_3_sum4,
       X0Y1_out, X0Y2_out, X0Y3_out, X1Y0_out, X1Y1_out, X1Y2_out, X2Y0_out, X2Y1_out, X2Y2_out, X2Y3_out,
       X3Y0_out, X3Y1_out, X3Y2_out, X3Y3_out;

  and X0Y3 (X0Y3_out, Y3, X0);
  and and_1 (and_1_out, X1, Y3);
  and X0Y2 (X0Y2_out, X0, Y2);
  and X1Y2 (X1Y2_out, X1, Y2);
  and X2Y2 (X2Y2_out, X2, Y2);
  and X3Y2 (X3Y2_out, Y2, X3);
  and X2Y3 (X2Y3_out, X2, Y3);
  and X3Y0 (X3Y0_out, X3, Y0);
  and X3Y1 (X3Y1_out, X3, Y1);
  and X3Y3 (X3Y3_out, X3, Y3);
  _4_bit_Ripple_Carry_Adder u_4_bit_ripple_carry_adder_1 (
    .Y3(X3Y2_out), .X3(n4_bit_ripple_carry_adder_3_sum4), .Y2(X2Y2_out),
    .X2(n4_bit_ripple_carry_adder_3_sum3), .Y1(X1Y2_out), .X1(n4_bit_ripple_carry_adder_3_sum2),
    .Y0(X0Y2_out), .X0(n4_bit_ripple_carry_adder_3_sum1), .Sum4(n4_bit_ripple_carry_adder_1_sum4),
    .Sum3(n4_bit_ripple_carry_adder_1_sum3), .Sum2(n4_bit_ripple_carry_adder_1_sum2),
    .Sum1(n4_bit_ripple_carry_adder_1_sum1), .Sum0(Z2));
  and X2Y0 (X2Y0_out, X2, Y0);
  and X2Y1 (X2Y1_out, X2, Y1);
  _4_bit_Ripple_Carry_Adder u_4_bit_ripple_carry_adder_2 (
    .Y3(X3Y3_out), .X3(n4_bit_ripple_carry_adder_1_sum4), .Y2(X2Y3_out),
    .X2(n4_bit_ripple_carry_adder_1_sum3), .Y1(and_1_out), .X1(n4_bit_ripple_carry_adder_1_sum2),
    .Y0(X0Y3_out), .X0(n4_bit_ripple_carry_adder_1_sum1), .Sum4(Z7), .Sum3(Z6), .Sum2(Z5), .Sum1(Z4),
    .Sum0(Z3));
  and X1Y1 (X1Y1_out, X1, Y1);
  and X1Y0 (X1Y0_out, X1, Y0);
  _4_bit_Ripple_Carry_Adder u_4_bit_ripple_carry_adder_3 (
    .Y3(X3Y1_out), .X3(1'b0), .Y2(X2Y1_out), .X2(X3Y0_out), .Y1(X1Y1_out), .X1(X2Y0_out), .Y0(X0Y1_out),
    .X0(X1Y0_out), .Sum4(n4_bit_ripple_carry_adder_3_sum4), .Sum3(n4_bit_ripple_carry_adder_3_sum3),
    .Sum2(n4_bit_ripple_carry_adder_3_sum2), .Sum1(n4_bit_ripple_carry_adder_3_sum1), .Sum0(Z1));
  and XOY0 (Z0, X0, Y0);
  and X0Y1 (X0Y1_out, X0, Y1);

  // Notes on the sheet:
  //   factor (4 bits)
  //   second factor (4 bits)
  //   product (8 bits)
  //   most significant (highest) bit
  //   least significant (lowest) bit
endmodule

module _3by2_divider (
  input  Y2,
  input  Y1,
  input  Y0,
  input  X1,
  input  X0,
  output Z2,
  output Z1,
  output Z0,
  output Error
);


  // Notes on the sheet:
  //   Dividend (3 bits: Y2 Y1 Y0)
  //   Divisor (2 bits: X1 X0)
  //   Quotient (4 bits: Z2 Z1 Z0 and Error)
endmodule
